# Fritzing sketch Water flow meter (saved by Fritzing 0.9.10b)
circuit board: 12.469cm x 5.9868cm
breadboards: 1

parts:
  Mod1 = Amica NodeMCU DEVKIT 1.0
  Part1 = LCD1602-I2C
  VCC1 = Battery block 9V
  U2 = Voltage Regulator - 5V [package="TO220 [THT]"]
  YF-S201_Flow_Meter2 = YF-S201 Water Flow Meter
  U3 = Voltage Regulator - 5V [package="TO220 [THT]"]

nets:
  N1: Mod1.pin1, Mod1.pin_10, Mod1.pin_26
  GND: Mod1.pin2, Mod1.pin_9, Mod1.pin_25, Mod1.pin_29, Part1.GND, YF-S201_Flow_Meter2.GND
  N2: Mod1.pin8, YF-S201_Flow_Meter2.SIG
  N3: Mod1.pin_13, Part1.SDA
  N4: Mod1.pin_14, Part1.SCL
  N5: Mod1.pin_30, U3.output_voltage
  VCC: Part1.VCC, U2.output_voltage, YF-S201_Flow_Meter2.VCC
  GND_2: VCC1.-, U2.GND, U3.GND
  N6: VCC1.+, U2.input_voltage, U3.input_voltage

custom parts:
  LCD1602-I2C: A standard character display, usually with 2x16 characters. Comes in many colors with LCM1602 IIC attached.
  YF-S201 Water Flow Meter: The YF-S201 Flow Meter. The input voltage is 5V to 24V (DC).

// code stored in the sketch: Completed Circuit Water Flow Meter.ino
#include<Wire.h>
#include<LiquidCrystal_I2C.h>
#include <ESP8266WiFi.h>;
#include <WiFiClient.h>;
#include <ThingSpeak.h>;

const char* ssid = "Connecting..............";   // Your Network SSID
const char* password = "iSiKawa_08";       // Your Network Password

WiFiClient client;

unsigned long myChannelNumber = 1766517; //Your Channel Number (Without Brackets)
const char * myWriteAPIKey = "1B77BZOAMITDYKLV"; //Your Write API Key


LiquidCrystal_I2C lcd(0x27,16,2);

int X;
int Y;
float TIME = 0;
float FREQUENCY = 0;
float WATER = 0;
float TOTAL = 0;
float LS = 0;
const int input = D5;




void setup()
{
Serial.begin(115200);

delay(10);
  // Connect to WiFi network
  WiFi.begin(ssid, password);
  ThingSpeak.begin(client);
 
lcd.begin();
lcd.backlight();
lcd.clear();
lcd.setCursor(0,0);
lcd.print("Water Flow Meter");
lcd.setCursor(0,1);
lcd.print("****************");
delay(2000);
pinMode(input,INPUT);
}


void loop()
{
X = pulseIn(input, HIGH);
Y = pulseIn(input, LOW);
TIME = X + Y;
FREQUENCY = 1000000/TIME;
WATER = FREQUENCY/7.5;
LS = WATER/60;
if(FREQUENCY >= 0)
{
if(isinf(FREQUENCY))
{
lcd.clear();
lcd.setCursor(0,0);
lcd.print("SPEED :0.00 L/M");
lcd.setCursor(0,1);
lcd.print("TOTAL:");
lcd.print( TOTAL);
lcd.print(" L");
ThingSpeak.writeField(myChannelNumber, 2,TOTAL, myWriteAPIKey);
Serial.println(TOTAL);

}
else
{
TOTAL = TOTAL + LS;
Serial.println(FREQUENCY);
lcd.clear();
lcd.setCursor(0,0);

//Print Speed in lcd
lcd.print("SPEED: ");
lcd.print(WATER);
lcd.print(" L/M");

//Print Speed in Serial monitor And server
Serial.print("Speed: ");
Serial.print(WATER);                 // Print on Serial Monitor
Serial.println(" L/M");
delay(1000);
//ThingSpeak.writeField(myChannelNumber, 1,WATER, myWriteAPIKey); //Update in ThingSpeak
ThingSpeak.writeField(myChannelNumber, 2,TOTAL, myWriteAPIKey); //Update in ThingSpeak
delay(100);

lcd.setCursor(0,1);

//Print total water in lcd
lcd.print("TOTAL:");
lcd.print( TOTAL);
lcd.print(" L");

//Print total water in S.Monitor and server
Serial.print("Total: ");
Serial.print(TOTAL);                 // Print on Serial Monitor
Serial.println(" L");
delay(1000);

delay(100);

}
}
delay(1000);
}
